// Logisim project Circuit2.circ as structural Verilog: 1 circuit, main circuit main
module main (
  input  ai,
  input  bi,
  input  in_3
);

  wire and_1_out, and_2_out, or_1_out, xor_1_out, xor_2_out;

  xor xor_1 (xor_1_out, ai, bi);
  and and_1 (and_1_out, xor_1_out, in_3);
  and and_2 (and_2_out, ai, bi);
  xor xor_2 (xor_2_out, xor_1_out, in_3);
  or or_1 (or_1_out, and_1_out, and_2_out);
endmodule
