// Logisim project Circuit3.circ as structural Verilog: 1 circuit, main circuit main
module main (
  input  ai,
  input  bi,
  input  T_i_1___I_i_1,
  input  _0_1_c,
  output si_di,
  output ti_Ii
);

  wire and_1_out, and_2_out, xor_1_out, xor_2_out, xor_4_out;

  xor xor_1 (xor_1_out, ai, bi);
  xor xor_2 (xor_2_out, ai, _0_1_c);
  xor xor_3 (si_di, xor_1_out, T_i_1___I_i_1);
  and and_1 (and_1_out, xor_2_out, ai);
  xor xor_4 (xor_4_out, xor_1_out, _0_1_c);
  and and_2 (and_2_out, xor_4_out, T_i_1___I_i_1);
  or or_1 (ti_Ii, and_1_out, and_2_out);

  // Notes on the sheet:
  //   (ai+c)bi
  //   (ai+bi)+ci
endmodule
