// Logisim project Circuit4.circ as structural Verilog: 1 circuit, main circuit main
module main (
  input  a,
  input  b,
  input  c,
  output M
);

  wire and_1_out, and_2_out, xor_1_out;

  xor xor_1 (xor_1_out, a, b);
  and and_1 (and_1_out, a, a);
  and and_2 (and_2_out, xor_1_out, c);
  or or_1 (M, and_2_out, and_1_out);
endmodule
