// Logisim project Decodor.circ as structural Verilog: 1 circuit, main circuit main
module main (
  input  b3,
  input  b2,
  input  b1,
  input  b0,
  output D0,
  output D1,
  output D2,
  output D3,
  output D4,
  output D5
);

  // Decoder #(.select(4), .enable("false")) decoder_1: pin names not known; wires that end beside it: {b3, b2, b1, b0}, D0, D1, D2, D3, D4, D5
endmodule
