// Logisim project Decodor3x8Cudoua2x4.circ as structural Verilog: 1 circuit, main circuit main
module main (
  input  a,
  input  b,
  input  c,
  output D0,
  output D1,
  output D2,
  output D3,
  output D4,
  output D5,
  output D6,
  output D7
);

  wire not_1_out;

  not not_1 (not_1_out, a);
  Decoder #(.select(2)) decoder_1 (.out0(D0), .out1(D1), .out2(D2), .out3(D3), .sel({b, c}), .en(not_1_out));
  Decoder #(.select(2)) decoder_2 (.out0(D4), .out1(D5), .out2(D6), .out3(D7), .sel({b, c}), .en(a));
endmodule
