// Logisim project LabPb3.circ as structural Verilog: 1 circuit, main circuit main
module main (
  input  D0,
  input  D1,
  input  C0,
  input  C1,
  input  C2,
  output f
);

  wire and_1_out, not_1_out, not_2_out, or_1_out, xnor_1_out, xor_1_out;

  not not_1 (not_1_out, D0);
  not not_2 (not_2_out, D1);
  and and_1 (and_1_out, D1, D0);
  or or_1 (or_1_out, D0, D1);
  xor xor_1 (xor_1_out, D0, D1);
  xnor xnor_1 (xnor_1_out, D0, D1);
  Multiplexer #(.select(3), .enable("false")) multiplexer_1 (
    .in0(D0), .in1(not_1_out), .in2(D1), .in3(not_2_out), .in4(and_1_out), .in5(or_1_out), .in6(xor_1_out),
    .in7(xnor_1_out), .out(f), .sel({C0, C1, C2}));
endmodule
