// Logisim project NumaratoareBinaraPe2Biti.circ as structural Verilog: 1 circuit, main circuit main
module main (
  input  CE,
  output A0,
  output A1,
  output OC
);

  wire and_1_out, clock_1_out;

  and and_1 (and_1_out, CE, A0);
  Clock clock_1 (.out(clock_1_out));
  and and_2 (OC, and_1_out, A1);
  J_K_Flip_Flop j_k_ff_1 (.J(CE), .clk(clock_1_out), .K(CE), .Q(A0));  // open: Qn, preset, en, reset
  J_K_Flip_Flop j_k_ff_2 (.J(and_1_out), .clk(clock_1_out), .K(and_1_out), .Q(A1));  // open: Qn, preset, en, reset
endmodule
