// Logisim project Pb2.circ as structural Verilog: 1 circuit, main circuit main
module main (
  input  I,
  input  CE,
  output O0,
  output O1,
  output O2,
  output O3
);

  wire [1:0] main_1_a0;

  Demultiplexer #(.select(2), .enable("false")) demultiplexer_1 (
    .out0(O0), .out1(O1), .out2(O2), .out3(O3), .in(I), .sel(main_1_a0));
  NumaratoareBinaraPe2Biti_main main_1 (.CE(CE), .A0(main_1_a0[0]), .A1(main_1_a0[1]));  // open: OC
endmodule
