// Logisim project Problema18.circ as structural Verilog: 1 circuit, main circuit main
module main (
  input  A,
  input  B,
  input  S,
  output C,
  output D
);

  Multiplexer #(.enable("false")) multiplexer_1 (.in0(B), .in1(A), .out(C), .sel(S));
  Multiplexer #(.enable("false")) multiplexer_2 (.in0(A), .in1(B), .out(D), .sel(S));
endmodule
