// Logisim project Problema1Seminar.circ as structural Verilog: 1 circuit, main circuit main
module main (
  input  x2,
  input  x1,
  input  x0,
  output y2,
  output y1,
  output y0
);

  Adder #(.width(1)) adder_1 (.a(x1), .b(x0), .out(y1), .cin(x2), .cout(y2));
  not not_1 (y0, x0);
endmodule
