// Logisim project Problema3.circ as structural Verilog: 1 circuit, main circuit main
module main (
  input  a,
  input  b,
  input  c,
  output I,
  output D
);

  wire main_1_d, main_1_i, main_2_i;

  Semiscazator_main main_1 (.a(a), .b(b), .i(main_1_i), .d(main_1_d));
  Semiscazator_main main_2 (.a(main_1_d), .b(c), .i(main_2_i), .d(D));
  or or_1 (I, main_1_i, main_2_i);

  // Notes on the sheet:
  //   i(a,b)
  //   d(a,b)
endmodule
