// Logisim project RegistruDeIncarcareParalela.circ as structural Verilog: 1 circuit, main circuit main
module main (
  input  Load,
  output A0
);

  wire and_1_out, and_2_out, not_1_out;

  not not_1 (not_1_out, Load);
  and and_1 (and_1_out, A0, not_1_out);
  // AND_Gate and_2 has open pins: out=and_2_out
  D_Flip_Flop d_ff_1 ();  // open: clk, D, Q, Qn, preset, en, reset
  D_Flip_Flop d_ff_2 ();  // open: clk, D, Q, Qn, preset, en, reset
  D_Flip_Flop d_ff_3 ();  // open: clk, D, Q, Qn, preset, en, reset
  D_Flip_Flop d_ff_4 (.Q(A0));  // open: clk, D, Qn, preset, en, reset
endmodule
