// Logisim project Semiscazator.circ as structural Verilog: 1 circuit, main circuit main
module main (
  input  a,
  input  b,
  output i,
  output d
);

  wire not_1_out;

  not not_1 (not_1_out, a);
  and and_1 (i, not_1_out, b);
  xor xor_1 (d, a, b);
endmodule
