// Logisim project pb5.circ as structural Verilog: 1 circuit, main circuit main
module main (
  input  a,
  input  b,
  input  c,
  input  d,
  output f1,
  output f2,
  output f3
);

  wire nand_1_out, nand_2_out, nand_3_out, nand_4_out, nand_5_out, nand_6_out, nand_7_out, nand_8_out,
       not_1_out, not_2_out, not_3_out, not_4_out;

  not not_1 (not_1_out, b);
  not not_2 (not_2_out, a);
  not not_3 (not_3_out, c);
  not not_4 (not_4_out, d);
  nand nand_1 (nand_1_out, not_2_out, not_1_out, c, d);
  nand nand_2 (nand_2_out, not_2_out, b, c, not_4_out);
  nand nand_3 (nand_3_out, a, not_1_out, not_3_out, d);
  nand nand_4 (nand_4_out, a, b, not_3_out, not_4_out);
  nand nand_5 (nand_5_out, a, b, c, d);
  nand nand_6 (nand_6_out, b, c, d);
  nand nand_7 (nand_7_out, not_2_out, not_3_out, not_4_out);
  nand nand_8 (nand_8_out, not_2_out, not_1_out);
  nand nand_9 (f1, nand_1_out, nand_2_out, nand_3_out, nand_4_out, nand_5_out);
  nand nand_10 (f2, nand_6_out, not_2_out);
  nand nand_11 (f3, nand_7_out, nand_8_out);
endmodule
