// Logisim project pb5b.circ as structural Verilog: 1 circuit, main circuit main
module main (
  input  a,
  input  b,
  input  c,
  input  d,
  output f1,
  output f2,
  output f3
);

  wire and_1_out, and_2_out, and_3_out, and_4_out, and_5_out, and_6_out, and_7_out, and_8_out, not_1_out,
       not_2_out, not_3_out, not_4_out, or_1_out, xor_1_out, xor_2_out, xor_3_out, xor_4_out;

  not not_1 (not_1_out, a);
  not not_2 (not_2_out, b);
  not not_3 (not_3_out, d);
  not not_4 (not_4_out, c);
  xor xor_1 (xor_1_out, b, d);
  xor xor_2 (xor_2_out, a, c);
  and and_1 (and_1_out, a, b, c, d);
  and and_2 (and_2_out, a, b);
  xor xor_3 (xor_3_out, a, b);
  xor xor_4 (xor_4_out, c, d);
  and and_3 (and_3_out, a, not_2_out);
  and and_4 (and_4_out, not_1_out, not_2_out);
  and and_5 (and_5_out, not_1_out, b, not_4_out, not_3_out);
  and and_6 (and_6_out, xor_1_out, xor_2_out);
  and and_7 (and_7_out, xor_3_out, c, d);
  or or_1 (or_1_out, xor_4_out, not_4_out, not_3_out);
  and and_8 (and_8_out, or_1_out, and_3_out);
  or or_2 (f1, and_6_out, and_1_out);
  or or_3 (f2, and_2_out, and_7_out, and_8_out);
  or or_4 (f3, and_4_out, and_5_out);
endmodule
